# Fritzing sketch jairmausu (saved by Fritzing 0.9.4)

parts:
  S1 = Momentary Switch [package=ksa_sealed_tac_switch]
  パーツ1 = InvenSense MPU6050
  U1 = ESP32-38PinWide [part_number=ESP32-38PinWide]
  S2 = Momentary Switch [package=ksa_sealed_tac_switch]
  R3 = Resistor [tolerance=±5% resistance=220 package=THT]
  S3 = Momentary Switch [package=ksa_sealed_tac_switch]
  R4 = Resistor [tolerance=±5% resistance=220 package=THT]
  R2 = Resistor [tolerance=±5% resistance=220 package=THT]

nets:
  GND: S1.3, パーツ1.GND, U1.GND, S2.3, S3.3
  N1: S1.4, U1.GPIO16, R3.Pin_1
  VCC: パーツ1.VCC, U1.VIN, R3.Pin_0, R4.Pin_0, R2.Pin_0
  N2: パーツ1.SCL, U1.GPIO22
  N3: パーツ1.SDA, U1.GPIO21
  N4: U1.GPIO17, S2.4, R2.Pin_1
  N5: U1.GPIO5, S3.4, R4.Pin_1

custom parts:
  ESP32-38PinWide: Generic 38-Pin ESP32 with wide format (only access to one side of pins on a breadboard) based on Stephen Lilley's HiLetgo ESP-WROOM-32 ESP32 ESP-32S Development Board.
